// Logisim project ALUBLOCK.circ as structural Verilog: 1 circuit, main circuit main
module main (
  input  DR_i,
  input  AC_i,
  input  AND,
  input  CLOCK,
  input  ADD,
  input  LD,
  input  DR,
  input  INPR,
  input  INPR_i,
  input  COM,
  input  CLEAR,
  input  SHR,
  input  AC_i_1,
  input  SHL,
  input  AC_i_1_2,
  output AC_i_2
);

  wire adder_1_out, AND_2_out, AND_3_out, AND_4_out, AND_5_out, AND_6_out, AND_7_out, AND_8_out, AND_9_out,
       AND_out, not_1_out, not_2_out, OR_out;

  Adder #(.width(1)) adder_1 (.a(AC_i), .b(DR_i), .out(adder_1_out));  // open: cin, cout
  not not_1 (not_1_out, AC_i);
  and u_AND (AND_out, AND, AC_i, DR_i);
  and AND_2 (AND_2_out, ADD, adder_1_out);
  and AND_3 (AND_3_out, DR, DR_i);
  and AND_4 (AND_4_out, INPR, INPR_i);
  and AND_5 (AND_5_out, COM, not_1_out);
  and AND_6 (AND_6_out, SHR, AC_i_1);
  and AND_7 (AND_7_out, SHL, AC_i_1_2);
  or OR (OR_out, AND_out, AND_2_out, AND_3_out, AND_4_out, AND_5_out, AND_6_out, AND_7_out);
  not not_2 (not_2_out, OR_out);
  and AND_8 (AND_8_out, LD, OR_out);
  and AND_9 (AND_9_out, not_2_out, LD);
  J_K_Flip_Flop j_k_ff_1 (
    .J(AND_8_out), .clk(CLOCK), .K(AND_9_out), .Q(AC_i_2), .reset(CLEAR));  // open: Qn, preset, en
endmodule
