// Logisim project MEMORY.circ as structural Verilog: 1 circuit, main circuit main
module main (
  input  [11:0] AD,
  input  [15:0] DATA,
  input  WRITE,
  input  CLOCK,
  input  READ,
  output [15:0] OUTPUT
);

  RAM #(.addrWidth(12), .dataWidth(16), .bus("separate")) ram_1 (
    .addr(AD), .din(DATA), .data(OUTPUT), .str(WRITE), .clk(CLOCK), .ld(READ));  // open: sel, clr
endmodule
